# Fritzing sketch tp1 (saved by Fritzing 0.9.3b)
breadboards: 1

parts:
  Componente1 = Arduino Uno (Rev3)
  LED3 = RGB LED (com. cathode, rgb) [package="5 mm [THT]"]

nets:
  N1: Componente1.D4, LED3.red_anode
  N2: Componente1.D5_PWM, LED3.green_anode
  N3: Componente1.D6_PWM, LED3.blue_anode
  N4: Componente1.GND, LED3.common_cathode

// code stored in the sketch: tp1_parte1morison_gobbi.ino
void setup() {
  // put your setup code here, to run once:
  Serial.begin(9600);
}

void cambiarColor(int color){
  switch(color){
    case 1:{pinMode(4,OUTPUT);//RED
            pinMode(5,INPUT);
            pinMode(6,INPUT);
            break;
            }
    case 2:{pinMode(6,OUTPUT);//AZUL
            pinMode(4,INPUT);
            pinMode(5,INPUT);
            break;
            }
    case 3:{pinMode(5,OUTPUT);//VERDE
            pinMode(6,INPUT);
            pinMode(4,INPUT);
            break;
            }
    case 4:{pinMode(4,OUTPUT);//VIOLETA
            pinMode(6,OUTPUT);
            pinMode(5,INPUT);
            break;
            }
    case 5:{pinMode(4,OUTPUT);//AMARILLO
            pinMode(5,OUTPUT);
            pinMode(6,INPUT);
            break;
            }
    case 6:{pinMode(5,OUTPUT);//CELESTE
            pinMode(6,OUTPUT);
            pinMode(4,INPUT);
            break;
            }
    case 7:{pinMode(4,OUTPUT);//BLANCO
            pinMode(5,OUTPUT);
            pinMode(6,OUTPUT);
            break;
            }
  }
          
}

void apagar() {
  pinMode(4,INPUT);
  pinMode(5,INPUT);
  pinMode(6,INPUT);  
}
void loop() {
  // put your main code here, to run repeatedly:
  //cambiarColor(1);
  //delay(1000);
  //cambiarColor(2);
  //delay(1000);
  //cambiarColor(3);
  //delay(1000);
  //cambiarColor(4);
  //delay(1000);
  //cambiarColor(5);
  //delay(1000);
  //cambiarColor(6);
  //delay(1000);
  //cambiarColor(7);
  //delay(1000);

  if(Serial.available()>0){
    int color = Serial.parseInt();
    cambiarColor(color);
    delay(1000);
    apagar();
  }

}
