# Fritzing sketch tp2_ldr (saved by Fritzing 0.9.3b)
breadboards: 1

parts:
  Componente1 = Arduino Uno (Rev3)
  R1 = Photocell (LDR) [package=THT]
  LED1 = LED - 5mm [color="Red (633nm)" package="5 mm [THT]"]
  LED3 = LED - 5mm [color="Yellow (595nm)" package="5 mm [THT]"]
  LED4 = LED - 5mm [color="Green (565nm)" package="5 mm [THT]"]
  R2 = Resistor [tolerance=±5% resistance=220 package="2010 [SMD]"]
  R4 = Resistor [tolerance=±5% resistance=220 package="2010 [SMD]"]
  R5 = Resistor [tolerance=±5% resistance=220 package="2010 [SMD]"]
  R6 = Resistor [tolerance=±5% resistance=220 package="2010 [SMD]"]

nets:
  N1: Componente1.A0, R1.pin_0, R2.Pin_0
  N2: Componente1.D2, LED3.anode
  N3: Componente1.D3_PWM, LED1.anode
  N4: Componente1.D4, LED4.anode
  N5: Componente1.5V, R1.pin_1
  N6: Componente1.GND, R2.Pin_1, R4.Pin_1, R5.Pin_1
  N7: LED1.cathode, R6.Pin_0
  N8: LED3.cathode, R5.Pin_0
  N9: LED4.cathode, R4.Pin_0

// code stored in the sketch: tp2_ldr_morison_blanc_sanchez_gobbi_romero.ino
#define sensor A0
#define ledverde 4 
#define ledrojo 3
#define ledama 2

void setup() {
  // put your setup code here, to run once:
  Serial.begin(9600);
  
  //pinMode(sensor, INPUT);
  pinMode(ledverde, OUTPUT); //comienza apagado
  pinMode(ledrojo, OUTPUT); //comienza apagado
  pinMode(ledama, OUTPUT); //comienza apagado
}

void luminosidad(){ //comienza apagado
  int sensorValue = analogRead(sensor);
  Serial.println(sensorValue);
  if(sensorValue< 400){
    digitalWrite(ledverde,HIGH);
    digitalWrite(ledrojo,LOW);
    digitalWrite(ledama,LOW);
  }

  if(sensorValue< 800 && sensorValue>400){
    digitalWrite(ledama,HIGH);
    digitalWrite(ledrojo,LOW);
    digitalWrite(ledverde,LOW);
  }
  if(sensorValue>800){
    digitalWrite(ledrojo,HIGH); 
    digitalWrite(ledverde,LOW);
    digitalWrite(ledama,LOW); 
  }  
}

void loop() {
  // put your main code here, to run repeatedly:
  
  luminosidad();
  delay(1000);
}
