# Fritzing sketch tp2 touch (saved by Fritzing 0.9.3b)

parts:
  Componente1 = Arduino Uno (Rev3)
  Grove_Touch_Sensor(P)2 = Grove Touch Sensor (P)

nets:
  GND: Componente1.GND, Grove_Touch_Sensor(P)2.GND
  N1: Componente1.D7, Grove_Touch_Sensor(P)2.SIG
  5V: Componente1.5V, Grove_Touch_Sensor(P)2.VCC

custom parts:
  Grove Touch Sensor (P): Touch sensor, Grove connector, panel mount.

// code stored in the sketch: tp2_morison_blanc_sanchez_gobbi_romero.ino
#define sensor 7
#define led 13

void setup() {
  // put your setup code here, to run once:
  pinMode(sensor, INPUT);
  pinMode(led, OUTPUT);
}

void sensortactil(){
  int sensorValue = digitalRead(sensor);
  if(sensorValue==1){
    digitalWrite(led,HIGH);
  }
  else{
    digitalWrite(led,LOW);
  }  
}

void loop() {
  // put your main code here, to run repeatedly:
  sensortactil();

}
