# Fritzing sketch tp2_pushButton (saved by Fritzing 0.9.3b)
breadboards: 1

parts:
  Componente1 = Arduino Uno (Rev3)
  LED1 = LED - 5mm [color="Green (570nm)" package="5 mm [THT]"]
  Grove1 = Grove Button
  R1 = Resistor [tolerance=±5% resistance=220 package=THT]

nets:
  N1: Componente1.D2, Grove1.SIG
  N2: Componente1.D6_PWM, LED1.anode
  5V: Componente1.5V, Grove1.VCC
  GND: Componente1.GND, Grove1.GND, R1.Pin_1
  N3: LED1.cathode, R1.Pin_0

// code stored in the sketch: tp2_pushButton_morison_blanc_sanchez_gobbi_romero.ino.ino
#define pinSender 10
#define pinInt 2

#define led 6

volatile int state = LOW;
volatile bool control = true;

void setup() {
  Serial.begin(9600);
  pinMode(led, OUTPUT);
  pinMode(pinSender, OUTPUT);
  pinMode(pinInt, INPUT);

  //RISING ----- LOW A HIGH
  //FALLING ---- HIGH A LOW
  attachInterrupt(digitalPinToInterrupt(pinInt),blink,RISING);
}

void loop() {
  activar();
}

void blink() {
  if(control){
    Serial.println("Se activo interrupcion");
    digitalWrite(led, HIGH);
    control = false;
  }
}

void activar(){
  interrupts(); 
  delay(1000);
  digitalWrite(led, LOW);
  noInterrupts();
  control = true;
}
