# Fritzing sketch tp2 thermistor (saved by Fritzing 0.9.3b)
breadboards: 1

parts:
  Componente1 = Arduino Uno (Rev3)
  R1 = Temperature Sensor (Thermistor) [thermistor_type=NTC package=THT]
  R2 = Resistor [tolerance=±5% resistance=220 package="0603 [SMD]"]

nets:
  N1: Componente1.A0, R1.pin_1, R2.Pin_0
  N2: Componente1.5V, R2.Pin_1
  N3: Componente1.GND, R1.pin_0

// code stored in the sketch: tp2_termistor_morison_blanc_sanchez_gobbi_romero.ino.ino
int ThermistorPin = 0;
int Vo;
float R1 = 10000;
float logR2, R2, T, Tc, Tf;
float c1 = 1.009249522e-03, c2 = 2.378405444e-04, c3 = 2.019202697e-07;

void setup() {
  Serial.begin(9600);
}

void loop() {

  Vo = analogRead(ThermistorPin);
  R2 = R1 * (1023.0 / (float)Vo - 1.0);
  logR2 = log(R2);
  T = (1.0 / (c1 + c2*logR2 + c3*logR2*logR2*logR2));
  Tc = T - 273.15;
  Tf = (Tc * 9.0)/ 5.0 + 32.0; 

  Serial.print("Temperature: "); 
  Serial.print(Tf);
  Serial.print(" F; ");
  Serial.print(Tc);
  Serial.println(" C");   

  delay(500);
}
