# Fritzing sketch tp2 ultrasonic (saved by Fritzing 0.9.3b)
breadboards: 1

parts:
  Componente1 = Arduino Uno (Rev3)
  hc-sr1 = hc-sr04

nets:
  N1: Componente1.D4, hc-sr1.Echo
  N2: Componente1.D5_PWM, hc-sr1.Trig
  5V: Componente1.5V, hc-sr1.VCC
  GND: Componente1.GND, hc-sr1.GND

// code stored in the sketch: tp2_ultrasound_morison_blanc_sanchez_gobbi_romero.ino.ino.ino
#include <NewPing.h>

/*Aqui se configuran los pines donde debemos conectar el sensor*/
#define TRIGGER_PIN  5
#define ECHO_PIN     4
#define MAX_DISTANCE 200

/*Crear el objeto de la clase NewPing*/
NewPing sonar(TRIGGER_PIN, ECHO_PIN, MAX_DISTANCE);

void setup() {
  Serial.begin(9600);
}

void loop() {
  // Esperar 1 segundo entre mediciones
  delay(1000);
  // Obtener medicion de tiempo de viaje del sonido y guardar en variable uS
  int uS = sonar.ping_median();
  // Imprimir la distancia medida a la consola serial
  Serial.print("Distancia: ");
  // Calcular la distancia con base en una constante
  Serial.print(uS / US_ROUNDTRIP_CM);
  Serial.println("cm");
}
