# Fritzing sketch tp3_1 (saved by Fritzing 0.9.3b)

parts:
  Componente1 = Arduino Uno (Rev3)

nets:
  N1: Componente1.D10_PWM/SS, Componente1.D2

// code stored in the sketch: tp3_1.ino
#define pinSender 10
#define pinInt 2

#define led 13

volatile int state = LOW;

void setup() {
  Serial.begin(9600);
  pinMode(led, OUTPUT);
  pinMode(pinSender, OUTPUT);
  pinMode(pinInt, INPUT);

  //RISING ----- LOW A HIGH
  //FALLING ---- HIGH A LOW
  attachInterrupt(digitalPinToInterrupt(pinInt),blink,FALLING);
}

void loop() {
  // put your main code here, to run repeatedly:
  digitalWrite(pinSender, HIGH);
  Serial.println("ALTO");
  delay(1000);
  digitalWrite(pinSender, LOW);
  Serial.println("BAJO");
  delay(1000);
}

void blink() {
  Serial.println("Entro a blink");
  state = !state;
  digitalWrite(led,state);
  delay(1000);
}
