# Fritzing sketch tp3_2 (saved by Fritzing 0.9.3b)

parts:
  Componente1 = Arduino Uno (Rev3)
  Grove1 = Grove Button

nets:
  N1: Componente1.D2, Grove1.SIG
  5V: Componente1.5V, Grove1.VCC
  GND: Componente1.GND, Grove1.GND

// code stored in the sketch: tp3_2.ino.ino
#define pinSender 10
#define pinInt 2

#define led 13

volatile int state = LOW;
volatile bool control = true;

void setup() {
  Serial.begin(9600);
  pinMode(led, OUTPUT);
  pinMode(pinSender, OUTPUT);
  pinMode(pinInt, INPUT);

  //RISING ----- LOW A HIGH
  //FALLING ---- HIGH A LOW
  attachInterrupt(digitalPinToInterrupt(pinInt),blink,RISING);
}

void loop() {
  activar();
}

void blink() {
  if(control){
    Serial.println("Se activo interrupcion");
    digitalWrite(led, HIGH);
    control = false;
  }
}

void activar(){
  interrupts(); 
  delay(1000);
  digitalWrite(led, LOW);
  noInterrupts();
  control = true;
}
