# Fritzing sketch tp3_3 (saved by Fritzing 0.9.3b)
breadboards: 1

parts:
  Componente1 = Arduino Uno (Rev3)
  LED1 = LED - 5mm [color="Red (633nm)" package="5 mm [THT]"]
  LED2 = LED - 5mm [color="Yellow (595nm)" package="5 mm [THT]"]
  LED3 = LED - 5mm [color="Green (570nm)" package="5 mm [THT]"]
  R1 = Resistor [tolerance=±5% resistance=220 package=THT]
  R2 = Resistor [tolerance=±5% resistance=220 package=THT]
  R3 = Resistor [tolerance=±5% resistance=220 package=THT]
  Grove1 = Grove Button

nets:
  GND: Componente1.GND, R1.Pin_1, R2.Pin_1, R3.Pin_1, Grove1.GND
  N1: Componente1.D2, Grove1.SIG
  N2: Componente1.D4, LED1.anode
  N3: Componente1.D5_PWM, LED2.anode
  N4: Componente1.D6_PWM, LED3.anode
  5V: Componente1.5V, Grove1.VCC
  N5: LED1.cathode, R3.Pin_0
  N6: LED2.cathode, R2.Pin_0
  N7: LED3.cathode, R1.Pin_0

// code stored in the sketch: tp3_3.ino
#define pinInt 2

#define verde 6
#define amarillo 5
#define rojo 4

volatile int state = LOW;
volatile bool control = true;
volatile int cont = 0;

void setup() {
  Serial.begin(9600);
  pinMode(pinInt, INPUT);
  pinMode(verde, OUTPUT);
  pinMode(amarillo, OUTPUT);
  pinMode(rojo, OUTPUT);

  //RISING ----- LOW A HIGH
  //FALLING ---- HIGH A LOW
  attachInterrupt(digitalPinToInterrupt(pinInt),blink,RISING);
}

void loop() {
  activar();
}

void blink() {
  if(control){
    //Serial.println("Se activo interrupcion");
    cont = cont+1;
    Serial.println(cont);
    control = false;
    if(cont>0 && cont<3){
      digitalWrite(verde, HIGH);
      digitalWrite(amarillo, LOW);
      digitalWrite(rojo, LOW);
    }
    else{
      if(cont<5){
      digitalWrite(verde, LOW);
      digitalWrite(amarillo, HIGH);
      digitalWrite(rojo, LOW);
    }
    else{
      if(cont<7){
      digitalWrite(verde, LOW);
      digitalWrite(amarillo, LOW);
      digitalWrite(rojo, HIGH);
    }
    else{
      cont = 0;
      digitalWrite(verde, LOW);
      digitalWrite(amarillo, LOW);
      digitalWrite(rojo, LOW);
    }
  }
}
}
}

void activar(){
  interrupts(); 
  delay(500);
  noInterrupts();
  control = true;
}
