# Fritzing sketch tp3_4 (saved by Fritzing 0.9.3b)
breadboards: 1

parts:
  M1 = fc-51 [package=THT]
  Componente1 = Arduino Uno (Rev3)

nets:
  N1: M1.pin1, Componente1.D2
  N2: M1.pin2, Componente1.GND
  N3: M1.pin3, Componente1.5V

// code stored in the sketch: tp3_4.ino
#define pinInt 2

volatile int state = LOW;

void setup() {
  // put your setup code here, to run once:
  Serial.begin(9600);

  pinMode(pinInt, INPUT);

  attachInterrupt(digitalPinToInterrupt(pinInt),pasaMano,FALLING); 
}

void loop() {
  if(state){
    delay(1000);
    attachInterrupt(digitalPinToInterrupt(pinInt),sacaMano,RISING);
    state=LOW;}
}

void pasaMano() {
  Serial.println("MAMAAAA");
  detachInterrupt(digitalPinToInterrupt(pinInt));
  state = HIGH;
}

void sacaMano(){  
  Serial.println("saca la mano de ahi carajo");
  detachInterrupt(digitalPinToInterrupt(pinInt));
  attachInterrupt(digitalPinToInterrupt(pinInt),pasaMAno,FALLING);
}
