# Fritzing sketch mediogiro (saved by Fritzing 0.9.3b)
breadboards: 1

parts:
  SERVO1 = Tower Pro SG90 servo [part_number=101246]
  Componente1 = Arduino Uno (Rev3)

nets:
  N1: SERVO1.Signal, Componente1.D10_PWM/SS
  +5V: SERVO1.+5V, Componente1.5V
  GND: SERVO1.GND, Componente1.GND

custom parts:
  Tower Pro SG90 servo: Original file by John De Cristofaro http://www.adafruit.com/products/1449 Adafruit Feedback Servo (Small) Edited by: e-radionica.com 28/9/2015

// code stored in the sketch: mediogirofor.ino
#include <Servo.h>
Servo motor;

void setup() {
  // put your setup code here, to run once:
  motor.attach(10);
  motor.write(0);
}

void loop() {
  // put your main code here, to run repeatedly:
  mover(0,170);
  mover(170,0);
}

void mover(int emp, int fin){
  if(emp<fin){
    for(int i=emp; i<= fin; i++){
      motor.write(i);
      delay(20);
    }
  }
  else{
    for(int i=emp; i>= fin; i--){
      motor.write(i);
      delay(20);
    }
  }
}
