# Fritzing sketch conInt (saved by Fritzing 0.9.3b)
breadboards: 1

parts:
  SERVO1 = Tower Pro SG90 servo [part_number=101246]
  Componente1 = Arduino Uno (Rev3)
  LED1 = LED - 5mm [color="Green (560nm)" package="5 mm [THT]"]
  R1 = Resistor [tolerance=±5% resistance=220 package=THT]
  S1 = Pushbutton [package="[THT]"]
  R2 = Resistor [tolerance=±5% resistance=10k package=THT]

nets:
  N1: SERVO1.Signal, Componente1.D10_PWM/SS
  +5V: SERVO1.+5V, Componente1.5V, S1.Pin_1, S1.Pin_2
  GND: SERVO1.GND, Componente1.GND, LED1.anode, R2.Pin_0
  N2: Componente1.D9_PWM, R1.Pin_1
  N3: Componente1.D2, S1.Pin_3, S1.Pin_4, R2.Pin_1
  N4: LED1.cathode, R1.Pin_0

custom parts:
  Tower Pro SG90 servo: Original file by John De Cristofaro http://www.adafruit.com/products/1449 Adafruit Feedback Servo (Small) Edited by: e-radionica.com 28/9/2015

// code stored in the sketch: conInt.ino
#include <Servo.h>
#define led 9
#define pinInt 2
Servo motor;
volatile int state = LOW;

void setup() {
  // put your setup code here, to run once:
  Serial.begin(9600);
  pinMode(led, OUTPUT);
  digitalWrite(led, LOW);
  attachInterrupt(digitalPinToInterrupt(pinInt),prenderLed,RISING);
  motor.attach(10);
  motor.write(0);
}

void loop() {
  // put your main code here, to run repeatedly:
  mover(0,170);
  mover(170,0);
}

void mover(int emp, int fin){
  if(emp<fin){
    for(int i=emp; i<= fin; i+=45){
      motor.write(i);
      delay(500);
    }
  }
  else{
    for(int i=emp; i>= fin; i-=45){
      motor.write(i);
      delay(500);
    }
  }
}

void prenderLed(){
  state = !state;
  digitalWrite(led, state);
}
