# Fritzing sketch movRandom (saved by Fritzing 0.9.3b)
breadboards: 1

parts:
  SERVO1 = Tower Pro SG90 servo [part_number=101246]
  Componente1 = Arduino Uno (Rev3)

nets:
  N1: SERVO1.Signal, Componente1.D9_PWM
  +5V: SERVO1.+5V, Componente1.5V
  GND: SERVO1.GND, Componente1.GND

custom parts:
  Tower Pro SG90 servo: Original file by John De Cristofaro http://www.adafruit.com/products/1449 Adafruit Feedback Servo (Small) Edited by: e-radionica.com 28/9/2015

// code stored in the sketch: movRandom.ino
#include <Servo.h>
Servo motor;

void setup() {
  // put your setup code here, to run once:
  Serial.begin(9600);
  motor.attach(9);
  motor.write(0);
}

void loop() {
  // put your main code here, to run repeatedly:
  int i = 0;
  while(i<3){
    motor.write(rand()%170);
    i++;
    delay(500);
  }
  Serial.println(motor.read());
  delay(1000);
}
