# Fritzing sketch ControlPote (saved by Fritzing 0.9.3b)
breadboards: 1

parts:
  R1 = Rotary Potentiometer (Small) [maximum_resistance=100kΩ package=THT]
  Componente1 = Arduino Uno (Rev3)
  SERVO1 = Tower Pro SG90 servo [part_number=101246]

nets:
  5V: R1.leg1, Componente1.5V, SERVO1.+5V
  N1: R1.wiper, Componente1.A1
  GND: R1.leg2, Componente1.GND, SERVO1.GND
  N2: Componente1.D9_PWM, SERVO1.Signal

custom parts:
  Tower Pro SG90 servo: Original file by John De Cristofaro http://www.adafruit.com/products/1449 Adafruit Feedback Servo (Small) Edited by: e-radionica.com 28/9/2015

// code stored in the sketch: ControlPote.ino.ino
#include <Servo.h>
#define pote A1
Servo motor;

void setup() {
  // put your setup code here, to run once:
  motor.attach(9);
  motor.write(0);
}

void loop() {
  // put your main code here, to run repeatedly:
  motor.write(map(analogRead(pote), 0, 1023, 0, 170));
}
