# Fritzing sketch Girasol (saved by Fritzing 0.9.3b)
breadboards: 1

parts:
  SERVO1 = Tower Pro SG90 servo [part_number=101246]
  Componente1 = Arduino Uno (Rev3)
  R1 = Resistor [tolerance=±5% resistance=220 package=THT]
  R2 = Photocell (LDR) [package=THT]

nets:
  N1: SERVO1.Signal, Componente1.D9_PWM
  +5V: SERVO1.+5V, Componente1.5V, R2.pin_0
  GND: SERVO1.GND, Componente1.GND, R1.Pin_1
  N2: Componente1.A0, R1.Pin_0, R2.pin_1

custom parts:
  Tower Pro SG90 servo: Original file by John De Cristofaro http://www.adafruit.com/products/1449 Adafruit Feedback Servo (Small) Edited by: e-radionica.com 28/9/2015

// code stored in the sketch: Girasol.ino
#include <Servo.h>
#define sensor A0
#define sol 975
Servo motor;

void setup() {
  // put your setup code here, to run once:
  Serial.begin(9600);
  pinMode(sensor, INPUT);
  motor.attach(9);
  motor.write(0);
}

void loop() {
  // put your main code here, to run repeatedly:
  int medIZQ = 0;
  int medDER = 0;
  int valor = analogRead(sensor);
  int posicion = motor.read();
  if(valor<sol){
		medIZQ = valor;
		motor.write(posicion+10);
		delay(500);
		medDER = analogReaad(sensor);

  }

    if(medDER>medIZQ){
      while((valor<sol)&&(motor.read()<170)){
        posicion += 5;
        motor.write(posicion);
        valor = analogRead(sensor);
        delay(500);
      }
    }
    else{
      while((valor<sol)&&(motor.read()>0)){
        posicion -= 5;
        motor.write(posicion);
        valor = analogRead(sensor);
        delay(500);
      }
    }
  }
  Serial.println(valor);
  delay(500);

}
