# Fritzing sketch Stepper (saved by Fritzing 0.9.3b)

parts:
  Componente1 = Arduino Uno (Rev3)
  BREAKOUT1 = ULN2003A breakout board
  MOTOR1 = 28BYJ-48 Stepper Motor

nets:
  N1: Componente1.D8, BREAKOUT1.In_4
  N2: Componente1.D9_PWM, BREAKOUT1.In_3
  N3: Componente1.D10_PWM/SS, BREAKOUT1.In_2
  N4: Componente1.D11_PWM/MOSI, BREAKOUT1.In_1
  5V: Componente1.5V, BREAKOUT1.+5V
  N5: Componente1.GND, BREAKOUT1.0V
  N6: BREAKOUT1.RED_wire, MOTOR1.RED
  N7: BREAKOUT1.ORANGE_wire, MOTOR1.ORANGE
  N8: BREAKOUT1.YELLOW_wire, MOTOR1.YELLOW
  N9: BREAKOUT1.PINK_wire, MOTOR1.PINK
  N10: BREAKOUT1.BLUE_wire, MOTOR1.BLUE

custom parts:
  ULN2003A breakout board: ULN2003A 7-way Darlington Transistor Driver on breakoutboard

// code stored in the sketch: paso-paso.ino
#define IN1  11
#define IN2  10
#define IN3  9
#define IN4  8

void setup() {
  // put your setup code here, to run once:
  pinMode(IN1, OUTPUT);
  pinMode(IN2, OUTPUT);
  pinMode(IN3, OUTPUT);
  pinMode(IN4, OUTPUT);
  digitalWrite(IN1, LOW);
  digitalWrite(IN2, LOW);
  digitalWrite(IN3, LOW);
  digitalWrite(IN4, LOW);
}

void loop() {
  // put your main code here, to run repeatedly:
  izquierda(100);
  delay(5000);
  derecha(150);
  delay(5000);
}

void izquierda(int angulo){
  for(int i=0;i<angulo;i++){
    digitalWrite(IN1, LOW);
    digitalWrite(IN2, LOW);
    digitalWrite(IN3, LOW);
    digitalWrite(IN4, HIGH);
    delayMicroseconds(5000);
    digitalWrite(IN1, LOW);
    digitalWrite(IN2, LOW);
    digitalWrite(IN3, HIGH);
    digitalWrite(IN4, LOW);
    delayMicroseconds(5000);
    digitalWrite(IN1, LOW);
    digitalWrite(IN2, HIGH);
    digitalWrite(IN3, LOW);
    digitalWrite(IN4, LOW);
    delayMicroseconds(5000);
    digitalWrite(IN1, HIGH);
    digitalWrite(IN2, LOW);
    digitalWrite(IN3, LOW);
    digitalWrite(IN4, LOW);
    delayMicroseconds(5000);
  }
}

void derecha(int angulo){
  for(int i=0;i<angulo;i++){
    digitalWrite(IN1, LOW);
    digitalWrite(IN2, LOW);
    digitalWrite(IN3, LOW);
    digitalWrite(IN4, HIGH);
    delayMicroseconds(5000);
    digitalWrite(IN1, LOW);
    digitalWrite(IN2, LOW);
    digitalWrite(IN3, HIGH);
    digitalWrite(IN4, LOW);
    delayMicroseconds(5000);
    digitalWrite(IN1, LOW);
    digitalWrite(IN2, HIGH);
    digitalWrite(IN3, LOW);
    digitalWrite(IN4, LOW);
    delayMicroseconds(5000);
    digitalWrite(IN1, HIGH);
    digitalWrite(IN2, LOW);
    digitalWrite(IN3, LOW);
    digitalWrite(IN4, LOW);
    delayMicroseconds(5000);
  }
}
