# Fritzing sketch GirarMotor (saved by Fritzing 0.9.3b)

parts:
  Componente1 = Arduino Uno (Rev3)
  M1 = DC Motor

nets:
  N1: Componente1.D2, M1.pin_2
  N2: Componente1.D3_PWM, M1.pin_1

// code stored in the sketch: girarMotor.ino
#define motor 3
#define motor2 2
void setup() {
  // put your setup code here, to run once:
  pinMode(motor, OUTPUT);
  pinMode(motor2, OUTPUT);
}

void loop() {
  // put your main code here, to run repeatedly:
  digitalWrite(motor2, HIGH);
  digitalWrite(motor,LOW);
  delay(5000);
  delay(0500);
  digitalWrite(motor, HIGH);
  digitalWrite(motor2,LOW);
  delay(5000);
  delay(0500);
}
