# Fritzing sketch DistanciaBuzzer (saved by Fritzing 0.9.3b)
breadboards: 1

parts:
  Componente1 = Arduino Uno (Rev3)
  Componente2 = SRF05 Ultrasonic Rangefinder
  J1 = Piezo Speaker

nets:
  N1: Componente1.D10_PWM/SS, J1.pin2
  N2: Componente1.D4, Componente2.Echo
  N3: Componente1.D5_PWM, Componente2.Trig
  5V: Componente1.5V, Componente2.VCC
  GND: Componente1.GND, Componente2.GND, J1.pin1

// code stored in the sketch: DistBuzzer.ino
#include <NewPing.h>

/*Aqui se configuran los pines donde debemos conectar el sensor*/
#define TRIGGER_PIN  5
#define ECHO_PIN     4
#define MAX_DISTANCE 200
#define buzzer 10

/*Crear el objeto de la clase NewPing*/
NewPing sonar(TRIGGER_PIN, ECHO_PIN, MAX_DISTANCE);

void setup() {
  Serial.begin(9600);
  pinMode(buzzer, OUTPUT);
}

void loop() {
  // Esperar 1 segundo entre mediciones
  //delay(1000);
  // Obtener medicion de tiempo de viaje del sonido y guardar en variable uS
  int uS = sonar.ping_median();
  int distancia = uS / US_ROUNDTRIP_CM;
  Serial.println("la distancia es: "+(String) distancia+" cm.");
  if(distancia>20){
    sonido(1000);
  }
  else{
    if(distancia<10){
      sonido(250);
    }
    else{
      sonido(750);
    }
  }
}

void sonido(int segundos){
  digitalWrite(buzzer, HIGH);
  delay(segundos);
  digitalWrite(buzzer, LOW);
}
