# Fritzing sketch Untitled Sketch (saved by Fritzing 0.9.3b)

parts:
  8x8_LED_Modul_mit_MAX1 = 8x8 LED Modul mit MAX7219 [package=THT]
  Componente1 = Arduino Uno (Rev3)

nets:
  N1: 8x8_LED_Modul_mit_MAX1.VCC_Eingang, Componente1.5V
  N2: 8x8_LED_Modul_mit_MAX1.GND_Eingang, Componente1.GND
  N3: 8x8_LED_Modul_mit_MAX1.DIN_Eingang, Componente1.D12/MISO
  N4: 8x8_LED_Modul_mit_MAX1.CS_Eingang, Componente1.D10_PWM/SS
  N5: 8x8_LED_Modul_mit_MAX1.CLK_Eingang, Componente1.D11_PWM/MOSI

// code stored in the sketch: sketch_jun24a.ino
#include <LedControlMS.h>
#define NumMatrix 1       // Cuantas matrices vamos a usar

LedControl lc=LedControl(12,11,10, NumMatrix);  // Creamos una instancia de LedControl

void setup()
   {
      for (int i=0; i< NumMatrix ; i++)
        {
           lc.shutdown(i,false);    // Activar las matrices
           lc.setIntensity(i,8);    // Poner el brillo a un valor intermedio
           lc.clearDisplay(i);      // Y borrar todo
        }
   }

void loop()
   {
        lc.writeString(0," Mona Alexis Hernan Seba ");
        delay(1000);
   }
