# Fritzing sketch oled (saved by Fritzing 0.9.3b)

parts:
  Componente1 = Arduino Uno (Rev3)
  Grove1 = Grove OLED 128x96

nets:
  N1: Componente1.A4/SDA, Grove1.SDA
  N2: Componente1.A5/SCL, Grove1.SCL
  5V: Componente1.5V, Grove1.VCC
  GND: Componente1.GND, Grove1.GND

// code stored in the sketch: sketch_jun22a.ino
#include <Wire.h>
#include <Adafruit_GFX.h>
#include <Adafruit_SSD1306.h>

#define OLED_RESET 4
Adafruit_SSD1306 display(OLED_RESET);


void setup() {
  // put your setup code here, to run once:

  // by default, we'll generate the high voltage from the 3.3v line internally! (neat!)
  display.begin(SSD1306_SWITCHCAPVCC, 0x3C);  // initialize with the I2C addr 0x3D (for the 128x64)
  // init done

  // Clear the buffer.
  display.clearDisplay();

  Serial.begin(9600);
}

void loop() {
  // put your main code here, to run repeatedly:
  
  display.clearDisplay(); // clear previous buffered data

  display.setTextColor(WHITE);

  // header
  display.setCursor(0,0);
  display.setTextSize(1);
  display.println("Arduino");

 
  // texto
  display.setCursor(35,18);
  display.setTextSize(2);
  display.println("MONA");
  display.display(); // update display

  delay(1000); // temp update interval
}
