# Fritzing sketch HibernarLeer (saved by Fritzing 0.9.3b)
breadboards: 1

parts:
  Componente1 = Arduino Uno (Rev3)
  R1 = Photocell (LDR) [package=THT]
  R2 = Resistor [tolerance=±5% resistance=10k package=THT]

nets:
  N1: Componente1.A0, R1.pin_0, R2.Pin_1
  N2: Componente1.5V, R1.pin_1
  N3: Componente1.GND, R2.Pin_0

// code stored in the sketch: HibernarLeerMayor.ino
#include <LowPower.h>
#define sensor A0
int mayor = 0;

void setup() {
  Serial.begin(9600);
}

void loop() {
  for(int i = 0; i <3; i++){
    LowPower.powerDown(SLEEP_8S, ADC_OFF, BOD_OFF); 
  }
  int sensorValue = analogRead(sensor);
  if (sensorValue > mayor){
    mayor = sensorValue;
  }
  
  Serial.println(mayor);
  delay(400);
}
