# Fritzing sketch conInt (saved by Fritzing 0.9.3b)
breadboards: 1

parts:
  Componente1 = Arduino Uno (Rev3)
  R1 = Resistor [tolerance=±5% resistance=220 package=THT]
  S1 = Pushbutton [package="[THT]"]
  LED1 = LED - 5mm [color="Red (633nm)" package="5 mm [THT]"]
  R2 = Resistor [tolerance=±5% resistance=10k package=THT]

nets:
  N1: Componente1.D10_PWM/SS, R1.Pin_1
  N2: Componente1.GND, LED1.cathode, R2.Pin_0
  N3: Componente1.D2, S1.Pin_3, S1.Pin_4, R2.Pin_1
  N4: Componente1.5V, S1.Pin_1, S1.Pin_2
  N5: R1.Pin_0, LED1.anode

// code stored in the sketch: conInterrupcion.ino
#include <LowPower.h>
#define boton 2
#define LED 13

volatile int state = LOW;

void setup() {
  // put your setup code here, to run once:
  pinMode(LED, OUTPUT);
  pinMode(boton, INPUT);
  Serial.begin(9600);

  attachInterrupt(digitalPinToInterrupt(boton),blink,FALLING);
}

void loop() {
  // put your main code here, to run repeatedly:
  LowPower.powerDown(SLEEP_8S,ADC_OFF,BOD_OFF);
}

void blink(){
  Serial.println("Entro a blink");
  state = !state;
  digitalWrite(LED,state);
  delay(1000);
}
