# Fritzing sketch SegOInt (saved by Fritzing 0.9.3b)
breadboards: 1

parts:
  Componente1 = Arduino Uno (Rev3)
  R1 = Resistor [tolerance=±5% resistance=220 package=THT]
  S1 = Pushbutton [package="[THT]"]
  LED1 = LED - 5mm [color="Red (633nm)" package="5 mm [THT]"]
  R2 = Resistor [tolerance=±5% resistance=10k package=THT]

nets:
  N1: Componente1.D10_PWM/SS, R1.Pin_1
  N2: Componente1.GND, LED1.cathode, R2.Pin_0
  N3: Componente1.D2, S1.Pin_3, S1.Pin_4, R2.Pin_1
  N4: Componente1.5V, S1.Pin_1, S1.Pin_2
  N5: R1.Pin_0, LED1.anode

// code stored in the sketch: conInterrupcion.ino
#include <LowPower.h>
#define pinInt 2
#define led 10

void setup() {
  // put your setup code here, to run once:
  Serial.begin(9600);
  pinMode(led, OUTPUT);
  pinMode(pinInt, INPUT);
  digitalWrite(led, LOW);
  attachInterrupt(digitalPinToInterrupt(pinInt),parpadear,RISING);
}

void loop() {
  // put your main code here, to run repeatedly:
  Serial.println("Dormido");
  delay(500);
  LowPower.powerDown(SLEEP_FOREVER, ADC_OFF, BOD_OFF);
  Serial.println("Despierto");
  delay(500);
}

void parpadear(){
  int state = digitalRead(led);
  delay(500);
  if(state){
    Serial.println("SE APAGO EL LED");
    delay(500);
  }else{
    Serial.println("SE PRENDIO EL LED");
    delay(500);
  }
  digitalWrite(led, !state);
}

// code stored in the sketch: SegOInt.ino
#include <LowPower.h>
#define boton 2
#define LED 13

volatile bool inter = false;

volatile int state = LOW;

void setup() {
  // put your setup code here, to run once:
  pinMode(boton, INPUT);
  pinMode(LED, OUTPUT);
  Serial.begin(9600);

  attachInterrupt(digitalPinToInterrupt(boton),blink,FALLING);
}

void loop() {
  // put your main code here, to run repeatedly: 
  Serial.println("Dormido");
  delay(400);
  LowPower.powerDown(SLEEP_4S,ADC_OFF,BOD_OFF);
  
  if(inter == false){
    Serial.println("Despertado al pasar 7 segundos");
    state = !state;
    digitalWrite(LED,state);
    delay(1000);
  }
  else{
    inter = false;
  }
  
}

void blink(){
  inter = true;
  Serial.println("Despertado por interrupcion");
  state = !state;
  digitalWrite(LED,state);
  delay(1000);
}
