# Fritzing sketch Arduino java (saved by Fritzing 0.9.3b)
breadboards: 1

parts:
  Componente1 = Arduino Uno (Rev3)
  LED1 = RGB LED (com. anode, rbg) [package="5 mm [THT]"]

nets:
  N1: Componente1.D4, LED1.red_cathode
  N2: Componente1.D5_PWM, LED1.green_cathode
  N3: Componente1.D6_PWM, LED1.blue_cathode
  N4: Componente1.5V, LED1.common_anode

// code stored in the sketch: arduino-java-1.ino
void setup() {
  // put your setup code here, to run once:
  Serial.begin(9600);
}

void cambiarColor(int color){
  switch(color){
    case 1:{pinMode(4,OUTPUT);//RED
            pinMode(5,INPUT);
            pinMode(6,INPUT);
            break;
            }
    case 2:{pinMode(6,OUTPUT);//AZUL
            pinMode(4,INPUT);
            pinMode(5,INPUT);
            break;
            }
    case 3:{pinMode(5,OUTPUT);//VERDE
            pinMode(6,INPUT);
            pinMode(4,INPUT);
            break;
            }
    case 4:{pinMode(4,OUTPUT);//VIOLETA
            pinMode(6,OUTPUT);
            pinMode(5,INPUT);
            break;
            }
    case 5:{pinMode(4,OUTPUT);//AMARILLO
            pinMode(5,OUTPUT);
            pinMode(6,INPUT);
            break;
            }
    case 6:{pinMode(5,OUTPUT);//CELESTE
            pinMode(6,OUTPUT);
            pinMode(4,INPUT);
            break;
            }
    case 7:{pinMode(4,OUTPUT);//BLANCO
            pinMode(5,OUTPUT);
            pinMode(6,OUTPUT);
            break;
            }
  }
          
}

void apagar() {
  pinMode(4,INPUT);
  pinMode(5,INPUT);
  pinMode(6,INPUT);  
}

void loop() {
  if(Serial.available()>0){
    int color = Serial.parseInt();
    cambiarColor(color);
    
  }
}
